// Logisim project addsub-impl.circ as structural Verilog: 1 circuit, main circuit main
module main (
  input  [7:0] B,
  input  sub,
  input  [7:0] A,
  output [7:0] Y
);

  wire [7:0] multiplexer_1_out, not_1_out;

  assign not_1_out = ~B;  // NOT_Gate not_1, 8 bits wide
  Multiplexer #(.width(8), .enable("false")) multiplexer_1 (
    .in0(B), .in1(not_1_out), .out(multiplexer_1_out), .sel(sub));
  Adder adder_1 (.a(multiplexer_1_out), .b(A), .out(Y), .cin(sub));  // open: cout

  // Notes on the sheet:
  //   Build an adder-subtractor using one 8 bit adder
endmodule
