// Logisim project dff-impl.circ as structural Verilog: 3 circuits, main circuit main
module main (
  input  clk,
  input  reset,
  input  D,
  input  en,
  output Q
);

  wire and_1_out, multiplexer_1_out;

  and and_1 (and_1_out, ~reset, D);  // AND_Gate
  Multiplexer #(.enable("false")) multiplexer_1 (.in0(Q), .in1(and_1_out), .out(multiplexer_1_out), .sel(en));
  simple_dff simple_dff_1 (.clk(clk), .D(multiplexer_1_out), .Q(Q));
endmodule

module sim (
  input  D,
  input  reset,
  input  en
);

  wire clk_out, main_1_q;

  Clock clk (.out(clk_out));
  main main_1 (.clk(clk_out), .reset(reset), .D(D), .en(en), .Q(main_1_q));
  LED Q (.in(main_1_q));
endmodule

module simple_dff (
  input  clk,
  input  D,
  output Q
);

  D_Flip_Flop d_ff_1 (.clk(clk), .D(D), .Q(Q));  // open: Qn, preset, en, reset
endmodule
