// Logisim project mux-impl.circ as structural Verilog: 1 circuit, main circuit main
module main (
  input  DIN0,
  input  DIN1,
  input  Sel,
  output DOUT
);

  wire and_1_out, and_2_out;

  and and_1 (and_1_out, DIN0, ~Sel);  // AND_Gate
  and and_2 (and_2_out, DIN1, Sel);
  or or_1 (DOUT, and_1_out, and_2_out);

  // Notes on the sheet:
  //   Build a 2-1 MUX using basic logic gates
endmodule
