// Logisim project ser2par-impl.circ as structural Verilog: 2 circuits, main circuit main
module main (
  input  clk,
  input  Sin,
  input  reset,
  output [3:0] Pout,
  output valid
);

  wire d_ff_1_q;
  wire [1:0] adder_1_out, counter_1_q;
  wire [3:0] bit_extender_1_out;

  Counter #(.width(2), .max('h3)) counter_1 (.Q(counter_1_q), .clk(clk));  // open: load, D, count, carry, clr
  D_Flip_Flop d_ff_1 (.clk(clk), .D(Sin), .Q(d_ff_1_q), .preset(reset));  // open: Qn, en, reset
  assign bit_extender_1_out = {{3{1'b0}}, d_ff_1_q};  // Bit_Extender bit_extender_1
  Adder #(.width(2)) adder_1 (.a(counter_1_q), .b(2'b11), .out(adder_1_out));  // open: cin, cout
  Shifter #(.width(4)) shifter_1 (.in(bit_extender_1_out), .\dist (adder_1_out), .out(Pout));

  // Notes on the sheet:
  //   Build a serial-to-parallel converter
  //   Taking the complement by adding 3
endmodule

module sim (
  input  in_1
);

  wire button_1_out, clock_1_out, main_1_valid;
  wire [3:0] main_1_pout;

  main main_1 (.Sin(in_1), .clk(clock_1_out), .Pout(main_1_pout), .valid(main_1_valid), .reset(button_1_out));
  Clock clock_1 (.out(clock_1_out));
  Button button_1 (.out(button_1_out));
  Hex_Digit_Display hex_digit_display_1 (.value(main_1_pout), .dp(main_1_valid));
endmodule
