// Logisim project sub-impl.circ as structural Verilog: 1 circuit, main circuit main
module main (
  input  a,
  input  b,
  input  cin,
  output cout,
  output d
);

  wire and_1_out, and_2_out, or_1_out;

  and and_1 (and_1_out, ~a, or_1_out);  // AND_Gate
  or or_1 (or_1_out, b, cin);
  and and_2 (and_2_out, a, b, cin);
  ExactlyOne xor_1 (.out(d), .in0(a), .in1(b), .in2(cin));
  or or_2 (cout, and_1_out, and_2_out);

  // Notes on the sheet:
  //   Build a subtractor using basic logic gates
endmodule
