// Logisim project alu.circ as structural Verilog: 1 circuit, main circuit ALU
module ALU (
  input  [31:0] Op1,
  input  [31:0] Op2,
  input  [3:0] op,
  output [31:0] Res
);

  wire comparator_1_lt, comparator_2_lt;
  wire [31:0] ADD, AND, OR, SLL, SLT, SLTU, SRL, SUB, XOR;

  assign AND = Op1 & Op2;  // AND_Gate and_1, 32 bits wide
  assign OR = Op1 | Op2;  // OR_Gate or_1, 32 bits wide
  Adder #(.width(32)) adder_1 (.a(Op1), .b(Op2), .out(ADD));  // open: cin, cout
  Shifter #(.width(32)) shifter_1 (.in(Op1), .\dist (Op2[4:0]), .out(SLL));
  Comparator #(.width(32)) comparator_1 (.a(Op1), .b(Op2), .lt(comparator_1_lt));  // open: gt, eq
  Comparator #(.width(32), .mode("unsigned")) comparator_2 (.a(Op1), .b(Op2), .lt(comparator_2_lt));  // open: gt, eq
  assign XOR = Op1 ^ Op2;  // XOR_Gate xor_1, 32 bits wide
  Shifter #(.width(32), .shift("lr")) shifter_2 (.in(Op1), .\dist (Op2[4:0]), .out(SRL));
  Subtractor #(.width(32)) subtractor_1 (.a(Op1), .b(Op2), .out(SUB));  // open: bin, bout
  assign SLT = {{31{1'b0}}, comparator_1_lt};  // Bit_Extender bit_extender_1
  assign SLTU = {{31{1'b0}}, comparator_2_lt};  // Bit_Extender bit_extender_2
  Multiplexer #(.select(4), .width(32), .enable("false")) multiplexer_1 (
    .in0(ADD), .in1(SLL), .in2(SLT), .in3(SLTU), .in4(XOR), .in5(SRL), .in6(OR), .in7(AND), .in8(SUB),
    .out(Res), .sel(op));  // open: in9, in10, in11, in12, in13, in14, in15

  // Other names for the same wires on the sheet: Shamt[4:0] = Op2[4:0]

  // Notes on the sheet:
  //   use lower five bits for shift amount:
endmodule
