// Logisim project dmem.circ as structural Verilog: 1 circuit, main circuit Dmem
module Dmem (
  input  [31:0] Addr,
  input  [31:0] Din,
  input  write,
  input  clk,
  output [31:0] Dout
);

  RAM #(.addrWidth(16), .dataWidth(32), .bus("separate")) ram_1 (
    .addr(Addr[17:2]), .din(Din), .data(Dout), .str(write), .clk(clk));  // open: sel, ld, clr
endmodule
