// Logisim project reg.circ as structural Verilog: 1 circuit, main circuit Reg
module Reg (
  input  [31:0] din,
  input  clk,
  input  write,
  input  [3:0] Rw_idx,
  input  [3:0] R1_idx,
  input  [3:0] R2_idx,
  output [31:0] R1,
  output [31:0] R2
);

  wire en0, en1, en2, en3, en4, en5, en6, en7, en8, en9, en10, en11, en12, en13, en14, en15;
  wire [31:0] R1_t, R2_t, R3, R4, R5, R6, R7, R8, R9, R10, R11, R12, R13, R14, R15;

  Demultiplexer #(.select(4), .enable("false")) demultiplexer_1 (
    .out0(en0), .out1(en1), .out2(en2), .out3(en3), .out4(en4), .out5(en5), .out6(en6), .out7(en7),
    .out8(en8), .out9(en9), .out10(en10), .out11(en11), .out12(en12), .out13(en13), .out14(en14),
    .out15(en15), .in(write), .sel(Rw_idx));
  Register #(.width(32)) u_R1 (.D(din), .en(en1), .Q(R1_t), .clk(clk));  // open: clr
  Register #(.width(32)) u_R2 (.D(din), .en(en2), .Q(R2_t), .clk(clk));  // open: clr
  Register #(.width(32)) u_R3 (.D(din), .en(en3), .Q(R3), .clk(clk));  // open: clr
  Register #(.width(32)) u_R4 (.D(din), .en(en4), .Q(R4), .clk(clk));  // open: clr
  Register #(.width(32)) u_R5 (.D(din), .en(en5), .Q(R5), .clk(clk));  // open: clr
  Register #(.width(32)) u_R6 (.D(din), .en(en6), .Q(R6), .clk(clk));  // open: clr
  Register #(.width(32)) u_R7 (.D(din), .en(en7), .Q(R7), .clk(clk));  // open: clr
  Multiplexer #(.select(4), .width(32), .enable("false")) multiplexer_1 (
    .in0({32{1'b0}}), .in1(R1_t), .in2(R2_t), .in3(R3), .in4(R4), .in5(R5), .in6(R6), .in7(R7), .in8(R8),
    .in9(R9), .in10(R10), .in11(R11), .in12(R12), .in13(R13), .in14(R14), .in15(R15), .out(R1), .sel(R1_idx));
  Register #(.width(32)) u_R8 (.D(din), .en(en8), .Q(R8), .clk(clk));  // open: clr
  Register #(.width(32)) u_R9 (.D(din), .en(en9), .Q(R9), .clk(clk));  // open: clr
  Register #(.width(32)) u_R10 (.D(din), .en(en10), .Q(R10), .clk(clk));  // open: clr
  Register #(.width(32)) u_R11 (.D(din), .en(en11), .Q(R11), .clk(clk));  // open: clr
  Register #(.width(32)) u_R12 (.D(din), .en(en12), .Q(R12), .clk(clk));  // open: clr
  Register #(.width(32)) u_R13 (.D(din), .en(en13), .Q(R13), .clk(clk));  // open: clr
  Register #(.width(32)) u_R14 (.D(din), .en(en14), .Q(R14), .clk(clk));  // open: clr
  Register #(.width(32)) u_R15 (.D(din), .en(en15), .Q(R15), .clk(clk));  // open: clr
  Multiplexer #(.select(4), .width(32), .enable("false")) multiplexer_2 (
    .in0({32{1'b0}}), .in1(R1_t), .in2(R2_t), .in3(R3), .in4(R4), .in5(R5), .in6(R6), .in7(R7), .in8(R8),
    .in9(R9), .in10(R10), .in11(R11), .in12(R12), .in13(R13), .in14(R14), .in15(R15), .out(R2), .sel(R2_idx));
endmodule
