// Logisim project riscv-loadstore.circ as structural Verilog: 5 circuits, main circuit main
module main (
  output out_1,
  output out_2,
  output halt,
  output [31:0] out_4,
  output [31:0] out_5,
  output [3:0] rd,
  output [3:0] rs1,
  output [3:0] rs2,
  output out_9,
  output out_10,
  output out_11,
  output out_12,
  output [31:0] Op1,
  output [31:0] Op2,
  output [3:0] op,
  output [31:0] Res
);

  wire button_1_out, comparator_1_eq;
  wire [31:0] alu_1_res, dmem_1_dout, icount, Imm, reg_1_r2;

  Clock clock_1 (.out(out_1));
  PC pc_1 (.Load(1'b0), .Addr(out_4), .clk(out_1), .reset(out_2));  // open: Din
  Hex_Digit_Display hex_digit_display_1 (.value(out_4[31:28]));  // open: dp
  Hex_Digit_Display hex_digit_display_2 (.value(out_5[31:28]));  // open: dp
  Counter #(.width(32), .max('hffffffff)) counter_1 (.Q(icount), .clk(out_1));  // open: load, D, count, carry, clr
  Button button_1 (.out(button_1_out));
  Hex_Digit_Display hex_digit_display_3 (.value(out_4[23:20]));  // open: dp
  Hex_Digit_Display hex_digit_display_4 (.value(out_4[27:24]));  // open: dp
  Hex_Digit_Display hex_digit_display_5 (.value(out_5[27:24]));  // open: dp
  Hex_Digit_Display hex_digit_display_6 (.value(out_5[23:20]));  // open: dp
  IMem imem_1 (.Addr(out_4), .Instr(out_5));
  Hex_Digit_Display hex_digit_display_7 (.value(out_4[19:16]));  // open: dp
  Hex_Digit_Display hex_digit_display_8 (.value(out_4[15:12]));  // open: dp
  Hex_Digit_Display hex_digit_display_9 (.value(out_5[19:16]));  // open: dp
  Hex_Digit_Display hex_digit_display_10 (.value(out_5[15:12]));  // open: dp
  Comparator #(.width(32), .mode("unsigned")) comparator_1 (
    .a(icount), .b({32{1'b0}}), .eq(comparator_1_eq));  // open: gt, lt
  Hex_Digit_Display hex_digit_display_11 (.value(out_4[11:8]));  // open: dp
  Hex_Digit_Display hex_digit_display_12 (.value(out_4[7:4]));  // open: dp
  Hex_Digit_Display hex_digit_display_13 (.value(out_5[11:8]));  // open: dp
  Hex_Digit_Display hex_digit_display_14 (.value(out_5[7:4]));  // open: dp
  or or_1 (out_2, comparator_1_eq, button_1_out);
  Hex_Digit_Display hex_digit_display_15 (.value(out_4[3:0]));  // open: dp
  Hex_Digit_Display hex_digit_display_16 (.value(out_5[3:0]));  // open: dp
  Decode decode_1 (
    .Instr(out_5), .Wr_idx(rd), .R1_idx(rs1), .R2_idx(rs2), .Imm(Imm), .write(out_9), .op(op),
    .ALUsrc(out_10), .load(out_11), .store(out_12));
  Reg reg_1 (.R1_idx(rs1), .R2_idx(rs2), .write(out_9), .Rw_idx(rd), .R1(Op1), .R2(reg_1_r2), .clk(out_1), .din(Res));
  Multiplexer #(.width(32), .enable("false")) multiplexer_1 (.in0(Imm), .in1(reg_1_r2), .out(Op2), .sel(out_10));
  Comparator #(.width(32), .mode("unsigned")) comparator_2 (.a(32'h7c), .b(icount), .eq(halt));  // open: gt, lt
  ALU alu_1 (.Op1(Op1), .Op2(Op2), .Res(alu_1_res), .op(op));
  Dmem dmem_1 (.Addr(alu_1_res), .Dout(dmem_1_dout), .write(out_12), .Din(reg_1_r2), .clk(out_1));
  Multiplexer #(.width(32), .enable("false")) multiplexer_2 (
    .in0(alu_1_res), .in1(dmem_1_dout), .out(Res), .sel(out_11));

  // Other names for the same wires on the sheet: ALUsrc = out_10; clk = out_1; Instr[31:0] = out_5; load = out_11;
  //   PC[31:0] = out_4; reset = out_2; store = out_12; write = out_9

  // Notes on the sheet:
  //   Current value of the program counter:
  //   Current instruction:
  //   Instruction counter and reset logic:
  //   reset button:
  //   Change the value of #instrs  to the number of instructions to execute during simulation
  //   #instrs:
endmodule

module Decode (
  input  [31:0] Instr,
  output [31:0] Imm,
  output [3:0] Wr_idx,
  output [3:0] R1_idx,
  output [3:0] R2_idx,
  output write,
  output [3:0] op,
  output ALUsrc,
  output load,
  output store
);

  wire or_1_out;
  wire [3:3] and_1_out;
  wire [11:0] multiplexer_1_out;

  Multiplexer #(.width(12), .enable("false")) multiplexer_1 (
    .in0(Instr[31:20]), .in1({Instr[31:25], Instr[11:7]}), .out(multiplexer_1_out), .sel(store));
  and and_1 (and_1_out[3], Instr[30], Instr[5]);
  Comparator #(.width(7)) comparator_1 (.a(Instr[6:0]), .b(7'b0000011), .eq(load));  // open: gt, lt
  Comparator #(.width(7)) comparator_2 (.a(Instr[6:0]), .b(7'b0100011), .eq(store));  // open: gt, lt
  assign Imm = {{20{multiplexer_1_out[11]}}, multiplexer_1_out};  // Bit_Extender bit_extender_1
  or or_1 (or_1_out, load, store);
  not not_1 (write, store);
  Multiplexer #(.width(4), .enable("false")) multiplexer_2 (
    .in0({and_1_out[3], Instr[14:12]}), .in1(4'b0000), .out(op), .sel(or_1_out));
  and and_2 (ALUsrc, ~store, Instr[5]);  // AND_Gate

  assign R1_idx = Instr[18:15];
  assign R2_idx = Instr[23:20];
  assign Wr_idx = Instr[10:7];

  // Other names for the same wires on the sheet: rd[3:0] = Instr[10:7]; funct7[6:0] = Instr[31:25];
  //   imm12[11:0] = Instr[31:20]; sub = Instr[30]; funct3[2:0] = Instr[14:12]; rs2[3:0] = Instr[23:20];
  //   opcode[6:0] = Instr[6:0]; sel_reg = Instr[5]; rs1[3:0] = Instr[18:15]
endmodule

module ALU (
  input  [31:0] Op1,
  input  [31:0] Op2,
  input  [3:0] op,
  output [31:0] Res
);

  wire comparator_1_lt, comparator_2_lt;
  wire [31:0] ADD, AND, OR, SLL, SLT, SLTU, SRA, SRL, SUB, XOR;

  assign AND = Op1 & Op2;  // AND_Gate and_1, 32 bits wide
  assign OR = Op1 | Op2;  // OR_Gate or_1, 32 bits wide
  Shifter #(.width(32), .shift("ar")) shifter_1 (.in(Op1), .\dist (Op2[4:0]), .out(SRA));
  Adder #(.width(32)) adder_1 (.a(Op1), .b(Op2), .out(ADD));  // open: cin, cout
  Shifter #(.width(32)) shifter_2 (.in(Op1), .\dist (Op2[4:0]), .out(SLL));
  Comparator #(.width(32)) comparator_1 (.a(Op1), .b(Op2), .lt(comparator_1_lt));  // open: gt, eq
  Comparator #(.width(32), .mode("unsigned")) comparator_2 (.a(Op1), .b(Op2), .lt(comparator_2_lt));  // open: gt, eq
  assign XOR = Op1 ^ Op2;  // XOR_Gate xor_1, 32 bits wide
  Shifter #(.width(32), .shift("lr")) shifter_3 (.in(Op1), .\dist (Op2[4:0]), .out(SRL));
  Subtractor #(.width(32)) subtractor_1 (.a(Op1), .b(Op2), .out(SUB));  // open: bin, bout
  assign SLT = {{31{1'b0}}, comparator_1_lt};  // Bit_Extender bit_extender_1
  assign SLTU = {{31{1'b0}}, comparator_2_lt};  // Bit_Extender bit_extender_2
  Multiplexer #(.select(4), .width(32), .enable("false")) multiplexer_1 (
    .in0(ADD), .in1(SLL), .in2(SLT), .in3(SLTU), .in4(XOR), .in5(SRL), .in6(OR), .in7(AND), .in8(SUB),
    .in13(SRA), .out(Res), .sel(op));  // open: in9, in10, in11, in12, in14, in15

  // Other names for the same wires on the sheet: Shamt[4:0] = Op2[4:0]
endmodule

module PC (
  input  [31:0] Din,
  input  Load,
  input  clk,
  input  reset,
  output [31:0] Addr
);

  wire [31:0] adder_1_out, multiplexer_1_out;

  Multiplexer #(.width(32), .enable("false")) multiplexer_1 (
    .in0(adder_1_out), .in1(Din), .out(multiplexer_1_out), .sel(Load));
  Register #(.width(32)) PC (.D(multiplexer_1_out), .Q(Addr), .clk(clk), .clr(reset));  // open: en
  Adder #(.width(32)) adder_1 (.a(32'h4), .b(Addr), .out(adder_1_out));  // open: cin, cout
endmodule

module ALUop (
  input  [2:0] funct3,
  input  [6:0] funct7,
  input  [6:0] opcode,
  output src,
  output [3:0] op
);

  wire and_1_out, and_2_out, comparator_1_eq, comparator_2_eq, comparator_3_eq, not_1_out, or_2_out, or_3_out;
  wire [3:3] rop;

  not not_1 (not_1_out, opcode[5]);
  and and_1 (and_1_out, funct7[5], opcode[5]);
  Comparator #(.width(3), .mode("unsigned")) comparator_1 (
    .a(funct3), .b(3'b101), .eq(comparator_1_eq));  // open: gt, lt
  and and_2 (and_2_out, comparator_1_eq, not_1_out);
  or or_1 (rop[3], and_2_out, and_1_out);
  Comparator #(.width(7)) comparator_2 (.a(opcode), .b(7'b0000011), .eq(comparator_2_eq));  // open: gt, lt
  Comparator #(.width(7)) comparator_3 (.a(opcode), .b(7'b0100011), .eq(comparator_3_eq));  // open: gt, lt
  Multiplexer #(.width(4), .enable("false")) multiplexer_1 (
    .in0({rop[3], funct3}), .in1(4'b0000), .out(op), .sel(or_2_out));
  or or_2 (or_2_out, comparator_2_eq, comparator_3_eq);
  or or_3 (or_3_out, not_1_out, or_2_out);
  not not_2 (src, or_3_out);

  // Other names for the same wires on the sheet: rop[2:0] = funct3
endmodule
