// Logisim project imem.circ as structural Verilog: 1 circuit, main circuit IMem
module IMem (
  input  [31:0] Addr,
  output [31:0] Instr
);

  RAM #(.addrWidth(16), .dataWidth(32), .bus("asynch")) ram_1 (.addr(Addr[17:2]), .data(Instr));  // open: sel, ld, clr
endmodule
