// Logisim project riscv-r.circ as structural Verilog: 4 circuits, main circuit main
module main (
  output out_1,
  output out_2,
  output halt,
  output [31:0] out_4,
  output [31:0] out_5,
  output [3:0] rd,
  output [3:0] rs1,
  output [3:0] rs2,
  output out_9,
  output out_10,
  output [31:0] Op1,
  output [31:0] Op2,
  output [3:0] op,
  output [31:0] Res
);

  wire button_1_out, comparator_1_eq;
  wire [31:0] icount, Imm, reg_1_r2;

  Clock clock_1 (.out(out_1));
  PC pc_1 (.Load(1'b0), .Addr(out_4), .clk(out_1), .reset(out_2));  // open: Din
  Hex_Digit_Display hex_digit_display_1 (.value(out_4[31:28]));  // open: dp
  Hex_Digit_Display hex_digit_display_2 (.value(out_5[31:28]));  // open: dp
  Counter #(.width(32), .max('hffffffff)) counter_1 (.Q(icount), .clk(out_1));  // open: load, D, count, carry, clr
  Button button_1 (.out(button_1_out));
  Hex_Digit_Display hex_digit_display_3 (.value(out_4[27:24]));  // open: dp
  Hex_Digit_Display hex_digit_display_4 (.value(out_4[23:20]));  // open: dp
  Hex_Digit_Display hex_digit_display_5 (.value(out_5[27:24]));  // open: dp
  Hex_Digit_Display hex_digit_display_6 (.value(out_5[23:20]));  // open: dp
  IMem imem_1 (.Addr(out_4), .Instr(out_5));
  Hex_Digit_Display hex_digit_display_7 (.value(out_4[19:16]));  // open: dp
  Hex_Digit_Display hex_digit_display_8 (.value(out_4[15:12]));  // open: dp
  Hex_Digit_Display hex_digit_display_9 (.value(out_5[19:16]));  // open: dp
  Hex_Digit_Display hex_digit_display_10 (.value(out_5[15:12]));  // open: dp
  Comparator #(.width(32), .mode("unsigned")) comparator_1 (
    .a(icount), .b({32{1'b0}}), .eq(comparator_1_eq));  // open: gt, lt
  Hex_Digit_Display hex_digit_display_11 (.value(out_4[7:4]));  // open: dp
  Hex_Digit_Display hex_digit_display_12 (.value(out_4[11:8]));  // open: dp
  Hex_Digit_Display hex_digit_display_13 (.value(out_5[11:8]));  // open: dp
  Hex_Digit_Display hex_digit_display_14 (.value(out_5[7:4]));  // open: dp
  or or_1 (out_2, comparator_1_eq, button_1_out);
  Hex_Digit_Display hex_digit_display_15 (.value(out_4[3:0]));  // open: dp
  Hex_Digit_Display hex_digit_display_16 (.value(out_5[3:0]));  // open: dp
  Decode decode_1 (
    .Instr(out_5), .Wr_idx(rd), .R1_idx(rs1), .R2_idx(rs2), .Imm(Imm), .write(out_9), .ALUop(op),
    .ALUsrc(out_10));
  Reg reg_1 (.R1_idx(rs1), .R2_idx(rs2), .write(out_9), .Rw_idx(rd), .R1(Op1), .R2(reg_1_r2), .clk(out_1), .din(Res));
  Multiplexer #(.width(32), .enable("false")) multiplexer_1 (.in0(Imm), .in1(reg_1_r2), .out(Op2), .sel(out_10));
  Comparator #(.width(32), .mode("unsigned")) comparator_2 (.a(32'h7c), .b(icount), .eq(halt));  // open: gt, lt
  ALU alu_1 (.Op1(Op1), .Op2(Op2), .Res(Res), .op(op));

  // Other names for the same wires on the sheet: ALUsrc = out_10; clk = out_1; Instr[31:0] = out_5; PC[31:0] = out_4;
  //   reset = out_2; write = out_9

  // Notes on the sheet:
  //   Current value of the program counter:
  //   Current instruction:
  //   Instruction counter and reset logic:
  //   reset button:
  //   Change the value of #instrs  to the number of instructions to execute during simulation
  //   #instrs:
endmodule

module Decode (
  input  [31:0] Instr,
  output [31:0] Imm,
  output [3:0] Wr_idx,
  output [3:0] R1_idx,
  output [3:0] R2_idx,
  output write,
  output [3:0] ALUop,
  output ALUsrc
);

  wire [3:0] bit_extender_2_out, bit_extender_3_out;

  assign Imm = {{20{1'b0}}, Instr[31:20]};  // Bit_Extender bit_extender_1
  assign bit_extender_2_out = {{1{1'b0}}, Instr[14:12]};  // Bit_Extender bit_extender_2
  assign bit_extender_3_out = {{1{1'b1}}, Instr[14:12]};  // Bit_Extender bit_extender_3
  Multiplexer #(.width(4), .enable("false")) multiplexer_1 (
    .in0(bit_extender_2_out), .in1(bit_extender_3_out), .out(ALUop), .sel(Instr[30]));

  assign ALUsrc = Instr[5];
  assign R1_idx = Instr[18:15];
  assign R2_idx = Instr[23:20];
  assign Wr_idx = Instr[10:7];
  assign write = 1'b1;

  // Other names for the same wires on the sheet: funct3[2:0] = Instr[14:12]; imm12[11:0] = Instr[31:20];
  //   rs2[3:0] = Instr[23:20]; funct7[6:0] = Instr[31:25]; opcode[6:0] = Instr[6:0]; immediate = Instr[5];
  //   rd[3:0] = Instr[10:7]; rs1[3:0] = Instr[18:15]

  // Notes on the sheet:
  //   Implement the decoder
endmodule

module ALU (
  input  [31:0] Op1,
  input  [31:0] Op2,
  input  [3:0] op,
  output [31:0] Res
);

  wire comparator_1_lt, comparator_2_lt;
  wire [4:0] bit_extender_1_out, bit_extender_2_out;
  wire [31:0] adder_1_out, and_1_out, bit_extender_3_out, bit_extender_4_out, or_1_out, shifter_1_out,
       shifter_2_out, subtractor_1_out, xor_1_out;

  Bit_Extender #(.in_width(32), .out_width(5)) bit_extender_1 (.in(Op2), .out(bit_extender_1_out));
  Bit_Extender #(.in_width(32), .out_width(5)) bit_extender_2 (.in(Op2), .out(bit_extender_2_out));
  Adder #(.width(32)) adder_1 (.a(Op1), .b(Op2), .out(adder_1_out));  // open: cin, cout
  Shifter #(.width(32)) shifter_1 (.in(Op1), .\dist (bit_extender_1_out), .out(shifter_1_out));
  Comparator #(.width(32)) comparator_1 (.a(Op1), .b(Op2), .lt(comparator_1_lt));  // open: gt, eq
  Comparator #(.width(32), .mode("unsigned")) comparator_2 (.a(Op1), .b(Op2), .lt(comparator_2_lt));  // open: gt, eq
  assign xor_1_out = Op1 ^ Op2;  // XOR_Gate xor_1, 32 bits wide
  Shifter #(.width(32), .shift("lr")) shifter_2 (.in(Op1), .\dist (bit_extender_2_out), .out(shifter_2_out));
  assign or_1_out = Op1 | Op2;  // OR_Gate or_1, 32 bits wide
  assign and_1_out = Op1 & Op2;  // AND_Gate and_1, 32 bits wide
  Subtractor #(.width(32)) subtractor_1 (.a(Op1), .b(Op2), .out(subtractor_1_out));  // open: bin, bout
  assign bit_extender_3_out = {{31{1'b0}}, comparator_1_lt};  // Bit_Extender bit_extender_3
  assign bit_extender_4_out = {{31{1'b0}}, comparator_2_lt};  // Bit_Extender bit_extender_4
  Multiplexer #(.select(4), .width(32), .enable("false")) multiplexer_1 (
    .in0(adder_1_out), .in1(shifter_1_out), .in2(bit_extender_3_out), .in3(bit_extender_4_out),
    .in4(xor_1_out), .in5(shifter_2_out), .in6(or_1_out), .in7(and_1_out), .in8(subtractor_1_out), .out(Res),
    .sel(op));  // open: in9, in10, in11, in12, in13, in14, in15

  // Notes on the sheet:
  //   Implement the ALU
endmodule

module PC (
  input  [31:0] Din,
  input  Load,
  input  clk,
  input  reset,
  output [31:0] Addr
);

  wire [31:0] adder_1_out, multiplexer_1_out;

  Multiplexer #(.width(32), .enable("false")) multiplexer_1 (
    .in0(adder_1_out), .in1(Din), .out(multiplexer_1_out), .sel(Load));
  Register #(.width(32)) PC (.D(multiplexer_1_out), .Q(Addr), .clk(clk), .clr(reset));  // open: en
  Adder #(.width(32)) adder_1 (.a(32'h4), .b(Addr), .out(adder_1_out));  // open: cin, cout
endmodule
